# Fritzing sketch Arduino Class Piezo Speaker (saved by Fritzing 0.8.7b)
breadboards: 1

parts:
  Arduino_Leonardo = Arduino Leonardo (Rev3b)
  J1 = Piezo Speaker

nets:
  N1: Arduino_Leonardo.D7, J1.pin2
  5V: Arduino_Leonardo.5V
  N2: Arduino_Leonardo.GND, J1.pin1
